# Fritzing sketch TestRadar (saved by Fritzing 0.9.4)
breadboards: 1

parts:
  Part1 = Arduino Uno (Rev3)
  HC-SR04_Sensor_1 = HC-SR04 Ultrasonic Distance Sensor
  HC-SR04_Sensor_2 = HC-SR04 Ultrasonic Distance Sensor
  LED1 = smd LED [color="White (6500K)" package="1206 [SMD]"]
  LED2 = smd LED [color="White (6500K)" package="1206 [SMD]"]
  R1 = Resistor [tolerance=±5% resistance=1k package=THT]
  R2 = Resistor [tolerance=±5% resistance=1k package=THT]

nets:
  N1: Part1.D9_PWM, HC-SR04_Sensor_2.ECHO
  N2: Part1.D10_PWM/SS, HC-SR04_Sensor_1.ECHO
  N3: Part1.D12/MISO, R2.Pin_0
  N4: Part1.D13/SCK, R1.Pin_0
  N5: Part1.D2, HC-SR04_Sensor_2.TRIG
  N6: Part1.D4, HC-SR04_Sensor_1.TRIG
  5V: Part1.5V, HC-SR04_Sensor_1.VCC, HC-SR04_Sensor_2.VCC
  GND: Part1.GND, HC-SR04_Sensor_1.GND, HC-SR04_Sensor_2.GND, LED1.cathode, LED2.cathode
  N7: LED1.anode, R1.Pin_1
  N8: LED2.anode, R2.Pin_1

custom parts:
  HC-SR04 Ultrasonic Distance Sensor: The HC-SR04 is an ultrasonic distance sensor. It is capable of providing measurement for ranges of 2cm to 400cm. The module operates at 5V.

// code stored in the sketch: TestRadar.ino
#include <NewPing.h>

#define NUM_RADAR     2   // Nombre de sensors utilitzats.
#define DISTANCIA_MAX 10 // Distància màxima de detecció en cm.

byte ledDavant =   12;
byte ledDarrere =  13;

byte distancia;

NewPing sonar[NUM_RADAR] = {   // Sensor object array.
  NewPing(4, 10, DISTANCIA_MAX), // Per cada sensor s'ha de definir el pin de trigger, el de echo i la distància màxima de detecció.
  NewPing(2, 9, DISTANCIA_MAX)
};

void setup() {
  pinMode(ledDavant, OUTPUT);
  pinMode(ledDarrere, OUTPUT);
  
  Serial.begin(9600); // Obre el monitor sèrie per veure els resultats.
}

void loop() {
  for (int i = 0; i < NUM_RADAR; i++) { // Fa un cicle per tots els sensors i mostra el seu valor.
    delay(250); // Pausa de 250ms entre peticions. Aquest valor no hauría de ser menor de 29ms
    distancia = sonar[i].ping_cm();
    if (distancia != 0 && distancia <= DISTANCIA_MAX) {
      digitalWrite(ledDavant + i, HIGH);
    } else {
      digitalWrite(ledDavant + i, LOW);
    }
    Serial.print("Radar nº ");
    Serial.print(i);
    Serial.print(" Mesurat: ");
    Serial.print(distancia);
    Serial.print("cm ");
    Serial.print("  /  ");
  }
  Serial.println();
}
